// Digital circuit A-B.dig as structural Verilog
module A_B (
  input  A2,
  input  A1,
  input  A0,
  input  B2,
  input  B1,
  input  B0,
  input  EN,
  output E,
  output R2,
  output R1,
  output R0
);

  wire and_1_out, and_2_out, comparator_1_eq, not_4_out, not_5_out, not_6_out, not_7_out, or_1_out;
  wire [2:0] add_1_s, add_2_s, not_1_out;

  not not_1 (not_1_out[2], B2);
  not not_2 (not_1_out[1], B1);
  not not_3 (not_1_out[0], B0);
  Add #(.Bits(3)) add_1 (.a(not_1_out), .b(3'b001), .c_i(1'b0), .s(add_1_s));  // open: c_o
  Comparator #(.Signed("true"), .Bits(3)) comparator_1 (
    .a({A2, A1, A0}), .b({B2, B1, B0}), .eq(comparator_1_eq));  // open: gt, lt
  not not_4 (not_4_out, comparator_1_eq);
  Add #(.Bits(3)) add_2 (.a({A2, A1, A0}), .b(add_1_s), .c_i(1'b0), .s(add_2_s));  // open: c_o
  not not_5 (not_5_out, A2);
  not not_6 (not_6_out, add_1_s[2]);
  and and_1 (and_1_out, not_4_out, not_5_out, not_6_out, add_2_s[2]);
  and and_2 (and_2_out, not_4_out, A2, add_1_s[2], not_7_out);
  not not_7 (not_7_out, add_2_s[2]);
  or or_1 (or_1_out, and_1_out, and_2_out);
  and and_3 (R2, EN, add_2_s[2]);
  and and_4 (R1, EN, add_2_s[1]);
  and and_5 (R0, add_2_s[0], EN);
  and and_6 (E, EN, or_1_out);

  // Notes on the sheet:
  //   EN: default 1
  //   Cambio de Signo
  //   Comparador
  //   Detecta Overflow
endmodule
