// Digital circuit Ax2.dig as structural Verilog
module Ax2 (
  input  A2,
  input  A1,
  input  A0,
  input  EN,
  output E_R3,
  output R2,
  output R1,
  output R0
);

  wire add_1_c_o, add_1_s, add_2_c_o, add_2_s, add_3_c_o, add_3_s;

  Add add_1 (.a(A2), .b(A2), .c_i(add_2_c_o), .s(add_1_s), .c_o(add_1_c_o));
  Add add_2 (.a(A1), .b(A1), .c_i(add_3_c_o), .s(add_2_s), .c_o(add_2_c_o));
  Add add_3 (.a(A0), .b(A0), .c_i(1'b0), .s(add_3_s), .c_o(add_3_c_o));
  and and_1 (E_R3, EN, add_1_c_o);
  and and_2 (R2, add_1_s, EN);
  and and_3 (R1, add_2_s, EN);
  and and_4 (R0, add_3_s, EN);
endmodule
