// Digital circuit C2aSM.dig as structural Verilog
module C2aSM (
  input  A2,
  input  A1,
  input  A0,
  input  EN,
  output E,
  output R2,
  output R1,
  output R0
);

  wire and_1_out, and_2_out, and_3_out, and_4_out, not_1_out, not_2_out, not_3_out, or_1_out;

  not not_1 (not_1_out, A2);
  not not_2 (not_2_out, A1);
  not not_3 (not_3_out, A0);
  and and_1 (and_1_out, not_2_out, A2);
  and and_2 (and_2_out, not_3_out, A1);
  and and_3 (and_3_out, A1, not_1_out);
  and and_4 (and_4_out, not_3_out, not_2_out, A2);
  or or_1 (or_1_out, and_1_out, and_2_out, and_3_out);
  and and_5 (E, EN, and_4_out);
  and and_6 (R2, EN, A2);
  and and_7 (R1, EN, or_1_out);
  and and_8 (R0, A0, EN);
endmodule
