// Digital circuit Comparador.dig as structural Verilog
module Comparador (
  input  A2,
  input  A1,
  input  A0,
  input  B2,
  input  B1,
  input  B0,
  input  EN,
  output R2,
  output R1,
  output R0
);

  wire and_1_out, and_2_out, and_3_out, and_4_out, and_5_out, and_6_out, and_7_out, comparator_1_eq,
       comparator_1_gt, comparator_1_lt, decoder_1_out_0, decoder_1_out_1, or_1_out, or_2_out, or_3_out;

  and and_1 (and_1_out, B2, A2);
  Decoder decoder_1 (.sel(and_1_out), .out_0(decoder_1_out_0), .out_1(decoder_1_out_1));
  Comparator #(.Signed("true"), .Bits(3)) comparator_1 (
    .a({A2, A1, A0}), .b({B2, B1, B0}), .gt(comparator_1_gt), .eq(comparator_1_eq), .lt(comparator_1_lt));
  and and_2 (and_2_out, decoder_1_out_0, comparator_1_gt);
  and and_3 (and_3_out, decoder_1_out_0, comparator_1_eq);
  and and_4 (and_4_out, comparator_1_lt, decoder_1_out_0);
  and and_5 (and_5_out, decoder_1_out_1, comparator_1_gt);
  and and_6 (and_6_out, decoder_1_out_1, comparator_1_eq);
  and and_7 (and_7_out, comparator_1_lt, decoder_1_out_1);
  and and_8 (R2, EN, or_1_out);
  and and_9 (R1, EN, or_2_out);
  or or_1 (or_1_out, and_4_out, and_7_out);
  or or_2 (or_2_out, and_3_out, and_6_out);
  and and_10 (R0, EN, or_3_out);
  or or_3 (or_3_out, and_2_out, and_5_out);
endmodule
