// Digital circuit alu.dig as structural Verilog
module alu (
  input  A2,
  input  A1,
  input  A0,
  input  B2,
  input  B1,
  input  B0,
  input  C2,
  input  C1,
  input  C0,
  output E,
  output R2,
  output R1,
  output R0
);

  wire a_b_1_e, a_b_1_r0, a_b_1_r1, a_b_1_r2, ax2_1_e_r3, ax2_1_r0, ax2_1_r1, ax2_1_r2, c2asm_1_e,
       c2asm_1_r0, c2asm_1_r1, c2asm_1_r2, comparador_1_r0, comparador_1_r1, comparador_1_r2,
       decoder_1_out_0, decoder_1_out_1, decoder_1_out_2, decoder_1_out_3, decoder_1_out_4, decoder_1_out_5,
       numeroprimo_1_r0, numeroprimo_1_r1, numeroprimo_1_r2, smac2_1_r0, smac2_1_r1, smac2_1_r2;

  Decoder #(.Selector_Bits(3)) decoder_1 (
    .sel({C2, C1, C0}), .out_0(decoder_1_out_0), .out_1(decoder_1_out_1), .out_2(decoder_1_out_2),
    .out_3(decoder_1_out_3), .out_4(decoder_1_out_4), .out_5(decoder_1_out_5));  // open: out_6, out_7
  SMaC2 smac2_1 (.A2(A2), .A1(A1), .A0(A0), .EN(decoder_1_out_0), .R2(smac2_1_r2), .R1(smac2_1_r1), .R0(smac2_1_r0));
  C2aSM c2asm_1 (
    .A2(A2), .A1(A1), .A0(A0), .EN(decoder_1_out_1), .E(c2asm_1_e), .R2(c2asm_1_r2), .R1(c2asm_1_r1),
    .R0(c2asm_1_r0));
  A_B a_b_1 (
    .A2(A2), .A1(A1), .A0(A0), .B2(B2), .B1(B1), .B0(B0), .EN(decoder_1_out_2), .E(a_b_1_e), .R2(a_b_1_r2),
    .R1(a_b_1_r1), .R0(a_b_1_r0));
  Comparador comparador_1 (
    .A2(A2), .A1(A1), .A0(A0), .B2(B2), .B1(B1), .B0(B0), .EN(decoder_1_out_3), .R2(comparador_1_r2),
    .R1(comparador_1_r1), .R0(comparador_1_r0));
  Ax2 ax2_1 (
    .A2(A2), .A1(A1), .A0(A0), .EN(decoder_1_out_4), .E_R3(ax2_1_e_r3), .R2(ax2_1_r2), .R1(ax2_1_r1),
    .R0(ax2_1_r0));
  numeroPrimo numeroprimo_1 (
    .A0(A0), .A1(A1), .A2(A2), .EN(decoder_1_out_5), .R2(numeroprimo_1_r2), .R1(numeroprimo_1_r1),
    .R0(numeroprimo_1_r0));
  or or_1 (E, c2asm_1_e, a_b_1_e, ax2_1_e_r3);
  or or_2 (R2, smac2_1_r2, c2asm_1_r2, a_b_1_r2, comparador_1_r2, ax2_1_r2, numeroprimo_1_r2);
  or or_3 (R1, smac2_1_r1, c2asm_1_r1, a_b_1_r1, comparador_1_r1, ax2_1_r1, numeroprimo_1_r1);
  or or_4 (R0, smac2_1_r0, c2asm_1_r0, a_b_1_r0, comparador_1_r0, ax2_1_r0, numeroprimo_1_r0);
endmodule
