// Digital circuit numeroPrimo.dig as structural Verilog
module numeroPrimo (
  input  A0,
  input  A1,
  input  A2,
  input  EN,
  output R2,
  output R1,
  output R0
);

  wire and_1_out, and_2_out, not_1_out, or_1_out;

  not not_1 (not_1_out, A2);
  and and_1 (and_1_out, A0, A2);
  and and_2 (and_2_out, A1, not_1_out);
  or or_1 (or_1_out, and_1_out, and_2_out);
  and and_3 (R0, EN, or_1_out);

  assign R1 = R0;
  assign R2 = R0;
endmodule
