// Digital circuit solucio.dig as structural Verilog
module solucio (
  input  A2,
  input  A1,
  input  A0,
  input  B2,
  input  B1,
  input  B0,
  input  C2,
  input  C1,
  input  C0,
  output E,
  output R2,
  output R1,
  output R0
);

  alu alu_1 (
    .A2(A2), .A1(A1), .A0(A0), .B2(B2), .B1(B1), .B0(B0), .C2(C2), .C1(C1), .C0(C0), .E(E), .R2(R2), .R1(R1),
    .R0(R0));

  // Notes on the sheet:
  //   Eliige opción:
endmodule
